# Fritzing sketch kkduinopinoutfzz (saved by Fritzing 1.0.5)
circuit board: 8.46667cm x 5.64444cm

parts:
  Part1 = NRF24L01+ Breakout Board
  M1 = DC Motor [voltage_(max)=6V voltage_(min)=3V]
  M2 = DC Motor [voltage_(max)=6V voltage_(min)=3V]
  Part3 = Arduino Nano (Rev3.0) (ICSP)
  Part2 = Motor Driver 1A Dual TB6612FNG
  VCC1 = Battery block 9V [internal_resistance=0.1Ω]
  VCC2 = Battery block 9V [internal_resistance=0.1Ω]

nets:
  GND: Part1.GND, Part3.GND, Part2.GND, VCC1.-, VCC2.-
  VCC: Part1.VCC, Part3.3V3
  N1: Part1.CE, Part3.D9
  N2: Part1.CS, Part3.D10
  N3: Part1.SCK, Part3.D13/SCK
  N4: Part1.MOSI, Part3.D11/MOSI
  N5: Part1.MISO, Part3.D12/MISO
  N6: M1.pin_1, Part2.A01
  N7: M1.pin_2, Part2.A02
  N8: M2.pin_1, Part2.B01
  N9: M2.pin_2, Part2.B02
  N10: Part3.D2, Part2.STBY
  N11: Part3.D3, Part2.AIN1
  N12: Part3.D4, Part2.AIN2
  N13: Part3.D5, Part2.PWMA
  N14: Part3.D6, Part2.PWMB
  N15: Part3.D7, Part2.BIN1
  N16: Part3.D8, Part2.BIN2
  5V: Part3.5V, Part2.VCC
  N17: Part2.VM, VCC1.+, VCC2.+
